# Fritzing sketch Fritzing_Artefaktgenerator_Teensy_3-2_260215 (saved by Fritzing 1.0.4)

parts:
  Teensy_3_1 = Teensy 3.1
  J1 = female pin header, 2 pins [form="♀ (female)"]
  J3 = female pin header, 2 pins [form="♀ (female)"]

nets:
  N1: Teensy_3_1.GND, J3.pin2
  N2: Teensy_3_1.A14/DAC, J1.pin2

notes:
  GND
  Signal
