# Fritzing sketch Fritzing_Digitalboard_Teensy_4-1_260215 (saved by Fritzing 1.0.4)
breadboards: 2

parts:
  Teensy_4_1 = Teensy 4.1
  ADC = Adafruit ADS1115 16Bit I2C ADC [part_number="Adafruit #1085"]
  Signal_Input = female pin header, 2 pins [form="♀ (female)"]
  GND = female pin header, 2 pins [form="♀ (female)"]
  R1 = Resistor [tolerance=±5% resistance=100 package="0603 [SMD]"]
  TFT = 2.8" SPI TFT Module [part_number=MSP2807]

nets:
  GND: Teensy_4_1.GND, Teensy_4_1.GND2#55, ADC.ADDR, ADC.GND, GND.pin1, GND.pin2, TFT.pin2, TFT.pin4
  N1: Teensy_4_1.D7, TFT.pin5
  N2: Teensy_4_1.D8, TFT.pin3
  N3: Teensy_4_1.D9, TFT.pin6
  N4: Teensy_4_1.D10, TFT.pin9
  N5: Teensy_4_1.D11, TFT.pin7
  VIN: Teensy_4_1.Vin, ADC.VDD, R1.Pin_0, TFT.pin1
  N6: Teensy_4_1.A12/D26, ADC.SDA
  N7: Teensy_4_1.A13/D27, ADC.SCL
  N8: ADC.AIN0, Signal_Input.pin1, Signal_Input.pin2
  N9: R1.Pin_1, TFT.pin8

notes:
  GND
  SIGNAL

custom parts:
  Teensy 4.1: The Teensy is a complete USB-based microcontoller development system, in a very small footprint, capable of implementing many types of projects. All programming is done via the USB port. No special programmer is needed, only a standard micro-USB cable and a PC or Macintosh with a USB port.
  Adafruit ADS1115 16Bit I2C ADC: For microcontrollers without an analog-to-digital converter or when you want a higher-precision ADC, the ADS1115 provides 16-bit precision at 860 samples/second over I2C. The chip can be configured as 4 single-ended input channels, or two differential channels. As a nice bonus, it even includes a programmable gain amplifier, up to x16, to help boost up smaller single/differential signals to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
  2.8" SPI TFT Module: A generic 2.8 inch LCD TFT 320x240 display with touchscreen and SD card slot. Uses the ILI9341 controller, like the Adafruit displays of this size uses.
